# Fritzing sketch photoresistor (saved by Fritzing 0.9.3b)
breadboards: 1

parts:
  Part2 = Adafruit Feather HUZZAH ESP8266 [part_number="Adafruit #2821"]
  R3 = Resistor [tolerance=±5% resistance=10k package="0402 [SMD]"]
  LED3 = LED - 5mm [color="Red (633nm)" package="5 mm [THT]"]
  R4 = Resistor [tolerance=±5% resistance=560 package=THT]
  R5 = PHOTOCELL [package=photocell]
  R6 = Resistor [tolerance=±5% resistance=330 package="0402 [SMD]"]
  R7 = Resistor [tolerance=±5% resistance=330 package="0402 [SMD]"]
  R8 = Resistor [tolerance=±5% resistance=330 package="0402 [SMD]"]

nets:
  N1: Part2.ADC, R6.Pin_1, R7.Pin_0, R8.Pin_0
  N2: Part2.GND, R3.Pin_0, R4.Pin_0, R7.Pin_1, R8.Pin_1
  N3: Part2.3.3V, R5.P$1
  N4: Part2.GPIO2, LED3.anode
  N5: R3.Pin_1, R5.P$2, R6.Pin_0
  N6: LED3.cathode, R4.Pin_1

custom parts:
  Adafruit Feather HUZZAH ESP8266: his is the Adafruit Feather HUZZAH ESP8266 - our take on an 'all-in-one' ESP8266 WiFi development board with built in USB and battery charging. Its an ESP8266 WiFi module with all the extras you need, ready to rock! We have other boards in the Feather family, check'em out here. At the Feather HUZZAH's heart is an ESP8266 WiFi microcontroller clocked at 80 MHz and at 3.3V logic. This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
